# Fritzing sketch Control (saved by Fritzing 0.9.3b)

parts:
  Part1 = Arduino Nano (Rev3.0)
  Part3 = DeuLigne 1.1 - The Snootlab's LCD shield for Arduino
  DS3231 = mystery part, 6 pins [chip_label=DS3231]
  4x_Relay = mystery part, 6 pins [chip_label="4x Relay"]
  LCD_Enable = mystery part, 1 pin [chip_label=LCD_EN]

nets:
  GND: Part1.GND, Part3.GND, DS3231.pin6, 4x_Relay.pin1
  N1: Part1.D2, DS3231.pin2
  N2: Part1.D4, 4x_Relay.pin5
  N3: Part1.D5, 4x_Relay.pin4
  N4: Part1.D6, 4x_Relay.pin3
  N5: Part1.D7, 4x_Relay.pin2
  N6: Part1.D8, Part3.D4
  N7: Part1.D9, Part3.D5
  N8: Part1.D10, Part3.D6
  N9: Part1.D11/MOSI, Part3.D7
  N10: Part1.D12/MISO, LCD_Enable.pin1
  5V: Part1.5V, Part3.+5V, DS3231.pin5, 4x_Relay.pin6
  N11: Part1.A5, DS3231.pin3
  N12: Part1.A4, DS3231.pin4
  N13: Part1.A0, Part3.A0
  N14: Part1.D13/SCK, Part3.RESET
